# Fritzing sketch MeadowPresence (saved by Fritzing 0.9.8b)
breadboards: 1

parts:
  Mod1 = Meadow F7 Micro
  Part1 = LCD1602-I2C
  LED3 = RGB LED - (4 legs) [package="5 mm [THT]"]

nets:
  GND: Mod1.GND, Part1.GND
  N1: Mod1.DO2, LED3.red_cathode
  N2: Mod1.DO3, LED3.green_cathode
  N3: Mod1.DO4, LED3.blue_cathode
  N4: Mod1.DO7, Part1.SDA
  N5: Mod1.DO8, Part1.SCL
  +5V: Mod1.+5V, Part1.VCC, LED3.common_anode

custom parts:
  LCD1602-I2C: A standard character display, usually with 2x16 characters. Comes in many colors with LCM1602 IIC attached.
